# Fritzing sketch Baby_R2_Board (saved by Fritzing 0.9.6b)
breadboards: 1

parts:
  U1 = NodeMCU V1.0
  Right_Leg = Basic Servo
  Head = Basic Servo
  Left_Leg = Basic Servo
  Q1 = TIP120 Hi-Current Darlington Transistor  # not connected
  SP1 = SPEAKER [package=pcb_mount_speaker]  # not connected

nets:
  N1: U1.D5, Left_Leg.pulse
  N2: U1.D6, Right_Leg.pulse
  N3: U1.D7, Head.pulse
  GND: Right_Leg.gnd, Head.gnd, Left_Leg.gnd
  VCC: Right_Leg.vcc, Head.vcc, Left_Leg.vcc

custom parts:
  NodeMCU V1.0: ESP8266 based NodeMCU
